// Logisim project control-logic.circ as structural Verilog: 1 circuit, main circuit control_logic
module control_logic (
  input  [31:0] Instruction,
  input  BrEq,
  input  BrLt,
  output PCSel,
  output RegWEn,
  output [2:0] ImmSel,
  output BrUn,
  output ASel,
  output BSel,
  output [3:0] ALUSel,
  output MemWEn,
  output [1:0] WBSel
);

  wire AUtype, Btype, comparator_10_eq, funct7_1, funct7_5, JItype, Jtype, Ltype, LUtype, Rtype, Stype;

  // Probe on funct7_5
  // Probe on funct7_1
  BitSelector #(.width(7)) bitselector_1 (.in(Instruction[31:25]), .out(funct7_5), .sel(3'b101));
  BitSelector #(.width(7)) bitselector_2 (.in(Instruction[31:25]), .out(funct7_1), .sel(3'b000));
  Comparator #(.width(7)) comparator_1 (.a(Instruction[6:0]), .b(7'b0010011), .eq(BSel));  // open: gt, lt
  Comparator #(.width(7)) comparator_2 (.a(Instruction[6:0]), .b(7'b0110011), .eq(Rtype));  // open: gt, lt
  Comparator #(.width(7)) comparator_3 (.a(Instruction[6:0]), .b(7'b1100011), .eq(Btype));  // open: gt, lt
  Comparator #(.width(7)) comparator_4 (.a(Instruction[6:0]), .b(7'b0000011), .eq(Ltype));  // open: gt, lt
  Comparator #(.width(7)) comparator_5 (.a(Instruction[6:0]), .b(7'b0100011), .eq(Stype));  // open: gt, lt
  Comparator #(.width(7)) comparator_6 (.a(Instruction[6:0]), .b(7'b1101111), .eq(Jtype));  // open: gt, lt
  Comparator #(.width(7)) comparator_7 (.a(Instruction[6:0]), .b(7'b1100111), .eq(JItype));  // open: gt, lt
  Comparator #(.width(7)) comparator_8 (.a(Instruction[6:0]), .b(7'b0010111), .eq(AUtype));  // open: gt, lt
  Comparator #(.width(7)) comparator_9 (.a(Instruction[6:0]), .b(7'b0110111), .eq(LUtype));  // open: gt, lt
  Comparator #(.width(3)) comparator_10 (.a(Instruction[14:12]), .b(3'b101), .eq(comparator_10_eq));  // open: gt, lt
  and and_1 (ALUSel[3], comparator_10_eq, BSel, funct7_5);

  assign ALUSel[2:0] = Instruction[14:12];
  assign RegWEn = 1'b1;

  // Other names for the same wires on the sheet: funct3[2:0] = Instruction[14:12]; InstData[24:0] = Instruction[31:7];
  //   opcode[6:0] = Instruction[6:0]; funct7[6:0] = Instruction[31:25]; Itype = BSel

  // Notes on the sheet:
  //   INPUTS to your circuit
  //   DON'T CHANGE THE LOCATIONS OF THE INPUTS AND OUTPUTS!
  //   OUTPUT from your circuit
endmodule
